// Logisim project The Project of COE.circ as structural Verilog: 7 circuits, main circuit Riyadh, Hassan,Abdullah 
// RegWrite
module Riyadh__Hassan_Abdullah (
  input  in_1,
  output [4:0] out_2,
  output [4:0] out_3,
  output [4:0] out_4,
  output out_5,
  output [22:0] Instuction_Cache,
  output [31:0] out_7,
  output [31:0] out_8,
  output [31:0] out_9,
  output [22:0] W_Bus,
  output [15:0] Cache_Address,
  output [22:0] Cache_Data_in,
  output [22:0] Cache_Data_out,
  output [5:0] Opcode,
  output [5:0] Func,
  output RegWrite,
  output MemWrite,
  output MemRead
);

  wire BEQ, button_1_out, Clock, Junp, pull_resistor_1_node, R_type, Reg_Dst, Write_back;
  wire [1:0] pc_control_1_selecter;
  wire [4:0] multiplexer_2_out;
  wire [15:0] undriven;
  wire [22:0] adder_1_out, ext_1_1_out__1, register_1_q;
  wire [31:0] immedaite_instraction_1_output, multiplexer_1_out;
  wire [31:23] B_RF, multiplexer_4_out, undriven_2;

  Control_Unit control_unit_1 (
    .Opcode(Opcode), .Jump(Junp), .BEQ(BEQ), .Reg_Dst(Reg_Dst), .MemWrite(MemWrite), .MemRead(MemRead),
    .Write_back(Write_back), .ALU_Src(out_5), .RegWrite(RegWrite), .R_type(R_type));
  Clock #(.highDuration(3200)) Clk (.out(Clock));
  PC_control pc_control_1 (.Selecter(pc_control_1_selecter), .JUMP(Junp), .BEQ(BEQ), .in_1(in_1));
  Multiplexer #(.select(2), .width(23), .enable("false")) multiplexer_1 (
    .in0(ext_1_1_out__1), .in1({Instuction_Cache[22:6], Func}), .in2(out_7[22:0]), .in3(adder_1_out),
    .out(multiplexer_1_out[22:0]), .sel(pc_control_1_selecter));
  Register #(.width(23)) register_1 (
    .D(multiplexer_1_out[22:0]), .Q(register_1_q), .clk(Clock), .clr(button_1_out));  // open: en
  EXT__1 ext_1_1 (.INPUT__1(register_1_q), .OUT__1(ext_1_1_out__1));
  Button button_1 (.out(button_1_out));
  Pull_Resistor #(.pull(1)) pull_resistor_1 (.node(pull_resistor_1_node));
  RAM #(.addrWidth(16), .dataWidth(23)) ram_1 (
    .addr(undriven), .data({Instuction_Cache[22:6], Func}), .ld(pull_resistor_1_node));  // open: sel, clk, clr
  Multiplexer #(.width(5), .enable("false")) multiplexer_2 (
    .in0(Instuction_Cache[20:16]), .in1(Instuction_Cache[15:11]), .out(multiplexer_2_out), .sel(Reg_Dst));
  Immedaite_instraction immedaite_instraction_1 (
    .Imm8({Instuction_Cache[7:6], Func}), .Output(immedaite_instraction_1_output[22:0]));
  Register_File register_file_1 (
    .RA({out_2[4:2], Instuction_Cache[22:21]}), .RB(Instuction_Cache[20:16]), .RW(multiplexer_2_out),
    .out_7(out_7[22:0]), .out_8(Cache_Data_in), .W_bus(W_Bus), .RegWrite(RegWrite), .Clock(Clock));
  Multiplexer #(.width(32), .enable("false")) multiplexer_3 (
    .in0({B_RF, Cache_Data_in}), .in1(immedaite_instraction_1_output), .out(out_8), .sel(out_5));
  Adder #(.width(23)) adder_1 (
    .a(ext_1_1_out__1), .b(immedaite_instraction_1_output[22:0]), .out(adder_1_out));  // open: cin, cout
  ALU alu_1 (.in_1(out_7[22:0]), .in_2(out_8[22:0]), .out_4({out_9[22:16], Cache_Address}), .Func(Func));
  RAM #(.addrWidth(16), .dataWidth(23), .bus("separate")) ram_2 (
    .addr(Cache_Address), .din(Cache_Data_in), .data(Cache_Data_out), .str(MemWrite), .clk(Clock),
    .ld(MemRead));  // open: sel, clr
  Multiplexer #(.width(32), .enable("false")) multiplexer_4 (
    .in0({undriven_2, Cache_Data_out}), .in1({out_9[31:16], Cache_Address}),
    .out({multiplexer_4_out, W_Bus}), .sel(Write_back));
  // Pins of 23 and 32 bits meet at multiplexer_1_out
  // Pins of 23 and 30 bits meet at multiplexer_1_out[29:0]
  // Pins of 23 and 32 bits meet at {out_9[31:16], Cache_Address}
  // Pins of 23 and 32 bits meet at {undriven_2, Cache_Data_out}
  // Pins of 23 and 32 bits meet at {B_RF, Cache_Data_in}
  // Pins of 23 and 32 bits meet at {Opcode, out_2[4:2], Instuction_Cache[22:6], Func}
  // Pins of 8 and 16 bits meet at {Instuction_Cache[15:6], Func}
  // Pins of 23 and 32 bits meet at out_7
  // Pins of 5 and 14 bits meet at {Opcode, out_2[4:2], Instuction_Cache[15:11]}
  // Pins of 23 and 32 bits meet at {multiplexer_4_out, W_Bus}
  // Pins of 23 and 32 bits meet at immedaite_instraction_1_output
  // Pins of 23 and 32 bits meet at out_8

  assign Instuction_Cache[5:0] = Func;
  assign out_2[1:0] = Instuction_Cache[22:21];
  assign out_3 = Instuction_Cache[20:16];
  assign out_4 = Instuction_Cache[15:11];
  assign out_9[15:0] = Cache_Address;

  // Other names for the same wires on the sheet: A[31:0] = out_7; A_RF[31:0] = out_7;
  //   ALU_Out[31:0] = {out_9[31:16], Cache_Address}; ALU_Src = out_5; B[31:0] = out_8; B_RF[22:0] = Cache_Data_in;
  //   ALU_Func[5:0] = Func; Zero = in_1

  // Notes on the sheet:
  //   IF = Instruction Fetch 
  //   Single Cycle CPU
  //   ID = Instruction Decode 
  //   EX = Execute Clculate 
  //   Next PC address 
  //   MEM = Memory Access
  //   Instuction Cache
  //   Riyadh Alzahrani
  //   Abdullah Alzamanan
  //   Hassan Alhafiz
  //   WB = Write Back
  //   Jump Traget Imm 26
  //   Imm 16
  //   Branch Target
  //   ALU result
  //   Data Cache
endmodule

module Register_File (
  input  [4:0] RA,
  input  [4:0] RB,
  input  [4:0] RW,
  input  [22:0] W_bus,
  input  RegWrite,
  input  Clock,
  output [22:0] out_7,
  output [22:0] out_8
);

  wire and_1_out, and_2_out, and_3_out, and_4_out, and_5_out, and_6_out, and_7_out, and_8_out, and_9_out,
       and_10_out, and_11_out, and_12_out, and_13_out, and_14_out, and_15_out, and_16_out, and_17_out,
       and_18_out, and_19_out, and_20_out, and_21_out, and_22_out, and_23_out, and_24_out, and_25_out,
       and_26_out, and_27_out, and_28_out, and_29_out, and_30_out, and_31_out, decoder_1_out1,
       decoder_1_out2, decoder_1_out3, decoder_1_out4, decoder_1_out5, decoder_1_out6, decoder_1_out7,
       decoder_1_out8, decoder_1_out9, decoder_1_out10, decoder_1_out11, decoder_1_out12, decoder_1_out13,
       decoder_1_out14, decoder_1_out15, decoder_1_out16, decoder_1_out17, decoder_1_out18, decoder_1_out19,
       decoder_1_out20, decoder_1_out21, decoder_1_out22, decoder_1_out23, decoder_1_out24, decoder_1_out25,
       decoder_1_out26, decoder_1_out27, decoder_1_out28, decoder_1_out29, decoder_1_out30, decoder_1_out31,
       decoder_2_out0, decoder_2_out1, decoder_2_out2, decoder_2_out3, decoder_2_out4, decoder_2_out5,
       decoder_2_out6, decoder_2_out7, decoder_2_out8, decoder_2_out9, decoder_2_out10, decoder_2_out11,
       decoder_2_out12, decoder_2_out13, decoder_2_out14, decoder_2_out15, decoder_2_out16, decoder_2_out17,
       decoder_2_out18, decoder_2_out19, decoder_2_out20, decoder_2_out21, decoder_2_out22, decoder_2_out23,
       decoder_2_out24, decoder_2_out25, decoder_2_out26, decoder_2_out27, decoder_2_out28, decoder_2_out29,
       decoder_2_out30, decoder_2_out31, decoder_3_out0, decoder_3_out1, decoder_3_out2, decoder_3_out3,
       decoder_3_out4, decoder_3_out5, decoder_3_out6, decoder_3_out7, decoder_3_out8, decoder_3_out9,
       decoder_3_out10, decoder_3_out11, decoder_3_out12, decoder_3_out13, decoder_3_out14, decoder_3_out15,
       decoder_3_out16, decoder_3_out17, decoder_3_out18, decoder_3_out19, decoder_3_out20, decoder_3_out21,
       decoder_3_out22, decoder_3_out23, decoder_3_out24, decoder_3_out25, decoder_3_out26, decoder_3_out27,
       decoder_3_out28, decoder_3_out29, decoder_3_out30, decoder_3_out31;
  wire [22:0] R1_q, R2_q, R3_q, R4_q, R5_q, R6_q, R7_q, R8_q, R9_q, R10_q, R11_q, R12_q, R13_q, R14_q, R15_q,
       R16_q, R17_q, R18_q, R19_q, R20_q, R21_q, R22_q, R23_q, R24_q, R25_q, R26_q, R27_q, R28_q, R29_q,
       R30_q, R31_q;
  wire [31:23] controlled_buffer_32_out, controlled_buffer_64_out, undriven, undriven_2;

  Decoder #(.select(5), .enable("false")) decoder_1 (
    .out1(decoder_1_out1), .out2(decoder_1_out2), .out3(decoder_1_out3), .out4(decoder_1_out4),
    .out5(decoder_1_out5), .out6(decoder_1_out6), .out7(decoder_1_out7), .out8(decoder_1_out8),
    .out9(decoder_1_out9), .out10(decoder_1_out10), .out11(decoder_1_out11), .out12(decoder_1_out12),
    .out13(decoder_1_out13), .out14(decoder_1_out14), .out15(decoder_1_out15), .out16(decoder_1_out16),
    .out17(decoder_1_out17), .out18(decoder_1_out18), .out19(decoder_1_out19), .out20(decoder_1_out20),
    .out21(decoder_1_out21), .out22(decoder_1_out22), .out23(decoder_1_out23), .out24(decoder_1_out24),
    .out25(decoder_1_out25), .out26(decoder_1_out26), .out27(decoder_1_out27), .out28(decoder_1_out28),
    .out29(decoder_1_out29), .out30(decoder_1_out30), .out31(decoder_1_out31), .sel(RW));  // open: out0
  and and_1 (and_1_out, decoder_1_out1, RegWrite);
  and and_2 (and_2_out, decoder_1_out2, RegWrite);
  and and_3 (and_3_out, decoder_1_out3, RegWrite);
  and and_4 (and_4_out, decoder_1_out4, RegWrite);
  and and_5 (and_5_out, decoder_1_out5, RegWrite);
  and and_6 (and_6_out, decoder_1_out6, RegWrite);
  and and_7 (and_7_out, decoder_1_out7, RegWrite);
  and and_8 (and_8_out, decoder_1_out8, RegWrite);
  and and_9 (and_9_out, decoder_1_out9, RegWrite);
  and and_10 (and_10_out, decoder_1_out10, RegWrite);
  and and_11 (and_11_out, decoder_1_out11, RegWrite);
  and and_12 (and_12_out, decoder_1_out12, RegWrite);
  and and_13 (and_13_out, decoder_1_out13, RegWrite);
  and and_14 (and_14_out, decoder_1_out14, RegWrite);
  and and_15 (and_15_out, decoder_1_out15, RegWrite);
  and and_16 (and_16_out, decoder_1_out16, RegWrite);
  and and_17 (and_17_out, decoder_1_out17, RegWrite);
  and and_18 (and_18_out, decoder_1_out18, RegWrite);
  and and_19 (and_19_out, decoder_1_out19, RegWrite);
  and and_20 (and_20_out, decoder_1_out20, RegWrite);
  and and_21 (and_21_out, decoder_1_out21, RegWrite);
  and and_22 (and_22_out, decoder_1_out22, RegWrite);
  and and_23 (and_23_out, decoder_1_out23, RegWrite);
  and and_24 (and_24_out, decoder_1_out24, RegWrite);
  and and_25 (and_25_out, decoder_1_out25, RegWrite);
  and and_26 (and_26_out, decoder_1_out26, RegWrite);
  and and_27 (and_27_out, decoder_1_out27, RegWrite);
  and and_28 (and_28_out, decoder_1_out28, RegWrite);
  and and_29 (and_29_out, decoder_1_out29, RegWrite);
  and and_30 (and_30_out, decoder_1_out30, RegWrite);
  and and_31 (and_31_out, decoder_1_out31, RegWrite);
  Register #(.width(23)) R1 (.D(W_bus), .en(and_1_out), .Q(R1_q), .clk(Clock));  // open: clr
  Register #(.width(23)) R2 (.D(W_bus), .en(and_2_out), .Q(R2_q), .clk(Clock));  // open: clr
  Register #(.width(23)) R3 (.D(W_bus), .en(and_3_out), .Q(R3_q), .clk(Clock));  // open: clr
  Register #(.width(23)) R4 (.D(W_bus), .en(and_4_out), .Q(R4_q), .clk(Clock));  // open: clr
  Register #(.width(23)) R5 (.D(W_bus), .en(and_5_out), .Q(R5_q), .clk(Clock));  // open: clr
  Register #(.width(23)) R6 (.D(W_bus), .en(and_6_out), .Q(R6_q), .clk(Clock));  // open: clr
  Register #(.width(23)) R7 (.D(W_bus), .en(and_7_out), .Q(R7_q), .clk(Clock));  // open: clr
  Register #(.width(23)) R8 (.D(W_bus), .en(and_8_out), .Q(R8_q), .clk(Clock));  // open: clr
  Register #(.width(23)) R9 (.D(W_bus), .en(and_9_out), .Q(R9_q), .clk(Clock));  // open: clr
  Register #(.width(23)) R10 (.D(W_bus), .en(and_10_out), .Q(R10_q), .clk(Clock));  // open: clr
  Register #(.width(23)) R11 (.D(W_bus), .en(and_11_out), .Q(R11_q), .clk(Clock));  // open: clr
  Register #(.width(23)) R12 (.D(W_bus), .en(and_12_out), .Q(R12_q), .clk(Clock));  // open: clr
  Register #(.width(23)) R13 (.D(W_bus), .en(and_13_out), .Q(R13_q), .clk(Clock));  // open: clr
  Register #(.width(23)) R14 (.D(W_bus), .en(and_14_out), .Q(R14_q), .clk(Clock));  // open: clr
  Register #(.width(23)) R15 (.D(W_bus), .en(and_15_out), .Q(R15_q), .clk(Clock));  // open: clr
  Register #(.width(23)) R16 (.D(W_bus), .en(and_16_out), .Q(R16_q), .clk(Clock));  // open: clr
  Register #(.width(23)) R17 (.D(W_bus), .en(and_17_out), .Q(R17_q), .clk(Clock));  // open: clr
  Register #(.width(23)) R18 (.D(W_bus), .en(and_18_out), .Q(R18_q), .clk(Clock));  // open: clr
  Register #(.width(23)) R19 (.D(W_bus), .en(and_19_out), .Q(R19_q), .clk(Clock));  // open: clr
  Register #(.width(23)) R20 (.D(W_bus), .en(and_20_out), .Q(R20_q), .clk(Clock));  // open: clr
  Register #(.width(23)) R21 (.D(W_bus), .en(and_21_out), .Q(R21_q), .clk(Clock));  // open: clr
  Register #(.width(23)) R22 (.D(W_bus), .en(and_22_out), .Q(R22_q), .clk(Clock));  // open: clr
  Register #(.width(23)) R23 (.D(W_bus), .en(and_23_out), .Q(R23_q), .clk(Clock));  // open: clr
  Register #(.width(23)) R24 (.D(W_bus), .en(and_24_out), .Q(R24_q), .clk(Clock));  // open: clr
  Register #(.width(23)) R25 (.D(W_bus), .en(and_25_out), .Q(R25_q), .clk(Clock));  // open: clr
  Register #(.width(23)) R26 (.D(W_bus), .en(and_26_out), .Q(R26_q), .clk(Clock));  // open: clr
  Register #(.width(23)) R27 (.D(W_bus), .en(and_27_out), .Q(R27_q), .clk(Clock));  // open: clr
  Register #(.width(23)) R28 (.D(W_bus), .en(and_28_out), .Q(R28_q), .clk(Clock));  // open: clr
  Register #(.width(23)) R29 (.D(W_bus), .en(and_29_out), .Q(R29_q), .clk(Clock));  // open: clr
  Register #(.width(23)) R30 (.D(W_bus), .en(and_30_out), .Q(R30_q), .clk(Clock));  // open: clr
  Register #(.width(23)) R31 (.D(W_bus), .en(and_31_out), .Q(R31_q), .clk(Clock));  // open: clr
  assign out_7 = decoder_2_out1 ? R1_q : 23'bz;  // Controlled_Buffer controlled_buffer_1
  assign out_7 = decoder_2_out2 ? R2_q : 23'bz;  // Controlled_Buffer controlled_buffer_2
  assign out_7 = decoder_2_out3 ? R3_q : 23'bz;  // Controlled_Buffer controlled_buffer_3
  assign out_7 = decoder_2_out4 ? R4_q : 23'bz;  // Controlled_Buffer controlled_buffer_4
  assign out_7 = decoder_2_out5 ? R5_q : 23'bz;  // Controlled_Buffer controlled_buffer_5
  assign out_7 = decoder_2_out6 ? R6_q : 23'bz;  // Controlled_Buffer controlled_buffer_6
  assign out_7 = decoder_2_out7 ? R7_q : 23'bz;  // Controlled_Buffer controlled_buffer_7
  assign out_7 = decoder_2_out8 ? R8_q : 23'bz;  // Controlled_Buffer controlled_buffer_8
  assign out_7 = decoder_2_out9 ? R9_q : 23'bz;  // Controlled_Buffer controlled_buffer_9
  assign out_7 = decoder_2_out10 ? R10_q : 23'bz;  // Controlled_Buffer controlled_buffer_10
  assign out_7 = decoder_2_out11 ? R11_q : 23'bz;  // Controlled_Buffer controlled_buffer_11
  assign out_7 = decoder_2_out12 ? R12_q : 23'bz;  // Controlled_Buffer controlled_buffer_12
  assign out_7 = decoder_2_out13 ? R13_q : 23'bz;  // Controlled_Buffer controlled_buffer_13
  assign out_7 = decoder_2_out14 ? R14_q : 23'bz;  // Controlled_Buffer controlled_buffer_14
  assign out_7 = decoder_2_out15 ? R15_q : 23'bz;  // Controlled_Buffer controlled_buffer_15
  assign out_7 = decoder_2_out16 ? R16_q : 23'bz;  // Controlled_Buffer controlled_buffer_16
  assign out_7 = decoder_2_out17 ? R17_q : 23'bz;  // Controlled_Buffer controlled_buffer_17
  assign out_7 = decoder_2_out18 ? R18_q : 23'bz;  // Controlled_Buffer controlled_buffer_18
  assign out_7 = decoder_2_out19 ? R19_q : 23'bz;  // Controlled_Buffer controlled_buffer_19
  assign out_7 = decoder_2_out20 ? R20_q : 23'bz;  // Controlled_Buffer controlled_buffer_20
  assign out_7 = decoder_2_out21 ? R21_q : 23'bz;  // Controlled_Buffer controlled_buffer_21
  assign out_7 = decoder_2_out22 ? R22_q : 23'bz;  // Controlled_Buffer controlled_buffer_22
  assign out_7 = decoder_2_out23 ? R23_q : 23'bz;  // Controlled_Buffer controlled_buffer_23
  assign out_7 = decoder_2_out24 ? R24_q : 23'bz;  // Controlled_Buffer controlled_buffer_24
  assign out_7 = decoder_2_out25 ? R25_q : 23'bz;  // Controlled_Buffer controlled_buffer_25
  assign out_7 = decoder_2_out26 ? R26_q : 23'bz;  // Controlled_Buffer controlled_buffer_26
  assign out_7 = decoder_2_out27 ? R27_q : 23'bz;  // Controlled_Buffer controlled_buffer_27
  assign out_7 = decoder_2_out28 ? R28_q : 23'bz;  // Controlled_Buffer controlled_buffer_28
  assign out_7 = decoder_2_out29 ? R29_q : 23'bz;  // Controlled_Buffer controlled_buffer_29
  assign out_7 = decoder_2_out30 ? R30_q : 23'bz;  // Controlled_Buffer controlled_buffer_30
  assign out_7 = decoder_2_out31 ? R31_q : 23'bz;  // Controlled_Buffer controlled_buffer_31
  assign {controlled_buffer_32_out, out_7} = decoder_2_out0 ? {undriven, {23{1'b0}}} : 32'bz;  // Controlled_Buffer controlled_buffer_32
  Decoder #(.select(5), .enable("false")) decoder_2 (
    .out0(decoder_2_out0), .out1(decoder_2_out1), .out2(decoder_2_out2), .out3(decoder_2_out3),
    .out4(decoder_2_out4), .out5(decoder_2_out5), .out6(decoder_2_out6), .out7(decoder_2_out7),
    .out8(decoder_2_out8), .out9(decoder_2_out9), .out10(decoder_2_out10), .out11(decoder_2_out11),
    .out12(decoder_2_out12), .out13(decoder_2_out13), .out14(decoder_2_out14), .out15(decoder_2_out15),
    .out16(decoder_2_out16), .out17(decoder_2_out17), .out18(decoder_2_out18), .out19(decoder_2_out19),
    .out20(decoder_2_out20), .out21(decoder_2_out21), .out22(decoder_2_out22), .out23(decoder_2_out23),
    .out24(decoder_2_out24), .out25(decoder_2_out25), .out26(decoder_2_out26), .out27(decoder_2_out27),
    .out28(decoder_2_out28), .out29(decoder_2_out29), .out30(decoder_2_out30), .out31(decoder_2_out31),
    .sel(RA));
  assign out_8 = decoder_3_out1 ? R1_q : 23'bz;  // Controlled_Buffer controlled_buffer_33
  assign out_8 = decoder_3_out2 ? R2_q : 23'bz;  // Controlled_Buffer controlled_buffer_34
  assign out_8 = decoder_3_out3 ? R3_q : 23'bz;  // Controlled_Buffer controlled_buffer_35
  assign out_8 = decoder_3_out4 ? R4_q : 23'bz;  // Controlled_Buffer controlled_buffer_36
  assign out_8 = decoder_3_out5 ? R5_q : 23'bz;  // Controlled_Buffer controlled_buffer_37
  assign out_8 = decoder_3_out6 ? R6_q : 23'bz;  // Controlled_Buffer controlled_buffer_38
  assign out_8 = decoder_3_out7 ? R7_q : 23'bz;  // Controlled_Buffer controlled_buffer_39
  assign out_8 = decoder_3_out8 ? R8_q : 23'bz;  // Controlled_Buffer controlled_buffer_40
  assign out_8 = decoder_3_out9 ? R9_q : 23'bz;  // Controlled_Buffer controlled_buffer_41
  assign out_8 = decoder_3_out10 ? R10_q : 23'bz;  // Controlled_Buffer controlled_buffer_42
  assign out_8 = decoder_3_out11 ? R11_q : 23'bz;  // Controlled_Buffer controlled_buffer_43
  assign out_8 = decoder_3_out12 ? R12_q : 23'bz;  // Controlled_Buffer controlled_buffer_44
  assign out_8 = decoder_3_out13 ? R13_q : 23'bz;  // Controlled_Buffer controlled_buffer_45
  assign out_8 = decoder_3_out14 ? R14_q : 23'bz;  // Controlled_Buffer controlled_buffer_46
  assign out_8 = decoder_3_out15 ? R15_q : 23'bz;  // Controlled_Buffer controlled_buffer_47
  assign out_8 = decoder_3_out16 ? R16_q : 23'bz;  // Controlled_Buffer controlled_buffer_48
  assign out_8 = decoder_3_out17 ? R17_q : 23'bz;  // Controlled_Buffer controlled_buffer_49
  assign out_8 = decoder_3_out18 ? R18_q : 23'bz;  // Controlled_Buffer controlled_buffer_50
  assign out_8 = decoder_3_out19 ? R19_q : 23'bz;  // Controlled_Buffer controlled_buffer_51
  assign out_8 = decoder_3_out20 ? R20_q : 23'bz;  // Controlled_Buffer controlled_buffer_52
  assign out_8 = decoder_3_out21 ? R21_q : 23'bz;  // Controlled_Buffer controlled_buffer_53
  assign out_8 = decoder_3_out22 ? R22_q : 23'bz;  // Controlled_Buffer controlled_buffer_54
  assign out_8 = decoder_3_out23 ? R23_q : 23'bz;  // Controlled_Buffer controlled_buffer_55
  assign out_8 = decoder_3_out24 ? R24_q : 23'bz;  // Controlled_Buffer controlled_buffer_56
  assign out_8 = decoder_3_out25 ? R25_q : 23'bz;  // Controlled_Buffer controlled_buffer_57
  assign out_8 = decoder_3_out26 ? R26_q : 23'bz;  // Controlled_Buffer controlled_buffer_58
  assign out_8 = decoder_3_out27 ? R27_q : 23'bz;  // Controlled_Buffer controlled_buffer_59
  assign out_8 = decoder_3_out28 ? R28_q : 23'bz;  // Controlled_Buffer controlled_buffer_60
  assign out_8 = decoder_3_out29 ? R29_q : 23'bz;  // Controlled_Buffer controlled_buffer_61
  assign out_8 = decoder_3_out30 ? R30_q : 23'bz;  // Controlled_Buffer controlled_buffer_62
  assign out_8 = decoder_3_out31 ? R31_q : 23'bz;  // Controlled_Buffer controlled_buffer_63
  assign {controlled_buffer_64_out, out_8} = decoder_3_out0 ? {undriven_2, {23{1'b0}}} : 32'bz;  // Controlled_Buffer controlled_buffer_64
  Decoder #(.select(5), .enable("false")) decoder_3 (
    .out0(decoder_3_out0), .out1(decoder_3_out1), .out2(decoder_3_out2), .out3(decoder_3_out3),
    .out4(decoder_3_out4), .out5(decoder_3_out5), .out6(decoder_3_out6), .out7(decoder_3_out7),
    .out8(decoder_3_out8), .out9(decoder_3_out9), .out10(decoder_3_out10), .out11(decoder_3_out11),
    .out12(decoder_3_out12), .out13(decoder_3_out13), .out14(decoder_3_out14), .out15(decoder_3_out15),
    .out16(decoder_3_out16), .out17(decoder_3_out17), .out18(decoder_3_out18), .out19(decoder_3_out19),
    .out20(decoder_3_out20), .out21(decoder_3_out21), .out22(decoder_3_out22), .out23(decoder_3_out23),
    .out24(decoder_3_out24), .out25(decoder_3_out25), .out26(decoder_3_out26), .out27(decoder_3_out27),
    .out28(decoder_3_out28), .out29(decoder_3_out29), .out30(decoder_3_out30), .out31(decoder_3_out31),
    .sel(RB));
  // Pins of 23 and 32 bits meet at {controlled_buffer_64_out, out_8}
  // Pins of 23 and 32 bits meet at {controlled_buffer_32_out, out_7}
  // Pins of 23 and 32 bits meet at {undriven, {23{1'b0}}}
  // Pins of 23 and 32 bits meet at {undriven_2, {23{1'b0}}}

  // Notes on the sheet:
  //   Bus W
  //   Bus A
  //   Bus B
endmodule

module ALU (
  input  [22:0] in_1,
  input  [22:0] in_2,
  input  [5:0] Func,
  output [22:0] out_4
);

  wire [22:0] ADD, SUB;

  Adder #(.width(23)) adder_1 (.a(in_1), .b(in_2), .out(ADD));  // open: cin, cout
  Subtractor #(.width(23)) subtractor_1 (.a(in_1), .b(in_2), .out(SUB));  // open: bin, bout
  Multiplexer #(.select(2), .width(23), .enable("false")) multiplexer_1 (
    .in0(in_2), .in1(in_2), .in2(ADD), .in3(SUB), .out(out_4), .sel({Func[5], Func[1]}));

  // Other names for the same wires on the sheet: A[22:0] = in_1; B[22:0] = in_2
endmodule

module Immedaite_instraction (
  input  [7:0] Imm8,
  output [22:0] Output
);


  assign {Output[22:11], Output[6:0]} = {{12{1'b0}}, Imm8[7:1]};
endmodule

module EXT__1 (
  input  [22:0] INPUT__1,
  output [22:0] OUT__1
);

  wire [29:0] adder_1_out;

  Adder #(.width(23)) adder_1 (.a(INPUT__1), .b(23'h1), .out({OUT__1[17:0], adder_1_out[4:0]}));  // open: cin, cout
  // Pins of 23 and 30 bits meet at {adder_1_out[29:28], OUT__1, adder_1_out[4:0]}
  // Pins of 23 and 30 bits meet at 30'h1
endmodule

module PC_control (
  input  in_1,
  input  BEQ,
  input  JUMP,
  output [1:0] Selecter
);

  and and_1 (Selecter[0], in_1, BEQ);

  assign Selecter[1] = JUMP;
endmodule

module Control_Unit (
  input  [5:0] Opcode,
  output Jump,
  output BEQ,
  output Reg_Dst,
  output MemWrite,
  output MemRead,
  output Write_back,
  output ALU_Src,
  output RegWrite,
  output R_type
);

  wire Addi_out;

  and u_R_type (R_type, ~Opcode[0], ~Opcode[1], ~Opcode[2], ~Opcode[3], ~Opcode[4], ~Opcode[5]);  // AND_Gate
  and Addi (Addi_out, ~Opcode[0], ~Opcode[1], ~Opcode[2], Opcode[3], ~Opcode[4], ~Opcode[5]);  // AND_Gate
  and LW (MemRead, ~Opcode[0], Opcode[1], ~Opcode[2], Opcode[3], ~Opcode[4], ~Opcode[5]);  // AND_Gate
  and SW (MemWrite, ~Opcode[0], ~Opcode[1], Opcode[2], Opcode[3], ~Opcode[4], ~Opcode[5]);  // AND_Gate
  and u_BEQ (BEQ, Opcode[0], ~Opcode[1], Opcode[2], Opcode[3], ~Opcode[4], ~Opcode[5]);  // AND_Gate
  and u_Jump (Jump, ~Opcode[0], Opcode[1], ~Opcode[2], ~Opcode[3], ~Opcode[4], ~Opcode[5]);  // AND_Gate
  nor nor_1 (ALU_Src, BEQ, R_type);
  or or_1 (RegWrite, MemRead, Addi_out, R_type);
  not not_1 (Write_back, MemRead);

  assign Reg_Dst = R_type;
endmodule
